// Logisim project Problem-01.circ as structural Verilog: 2 circuits, main circuit 1.1(Drag & drop)
module _1_1_Drag___drop (
  input  A,
  input  B,
  input  C,
  input  D,
  output F
);

  wire M2_out, M6_out, M8_out, M9_out, M10_out, M12_out, M14_out, not_1_out, not_2_out, not_3_out, not_4_out;

  not not_1 (not_1_out, A);
  not not_2 (not_2_out, B);
  not not_3 (not_3_out, C);
  not not_4 (not_4_out, D);
  or M2 (M2_out, not_1_out, not_2_out, C, not_4_out);
  or M6 (M6_out, not_1_out, B, C, not_4_out);
  or M8 (M8_out, A, not_2_out, not_3_out, not_4_out);
  or M9 (M9_out, A, not_2_out, not_3_out, D);
  and and_1 (F, M2_out, M6_out, M8_out, M9_out, M10_out, M12_out, M14_out);
  or M10 (M10_out, A, not_2_out, C, not_4_out);
  or M12 (M12_out, A, B, not_3_out, not_4_out);
  or M14 (M14_out, A, B, C, not_4_out);

  // Notes on the sheet:
  //   1. (Drag & drop) F = POS( 2,6,8,9,10,12,14 )
endmodule

module _1_2_Analyse_Circuit (
  input  A,
  input  B,
  input  C,
  input  D,
  output F
);

  wire not_1_out, not_2_out, not_3_out, or_1_out, or_2_out, or_3_out;

  not not_1 (not_1_out, C);
  not not_2 (not_2_out, A);
  not not_3 (not_3_out, A);
  or or_1 (or_1_out, not_1_out, D);
  or or_2 (or_2_out, not_2_out, B, C);
  or or_3 (or_3_out, not_3_out, D);
  and and_1 (F, or_1_out, or_2_out, or_3_out);

  // Notes on the sheet:
  //   1. (Analyse) F = POS( 2,6,8,9,10,12,14 )
endmodule
