// Logisim project Problem-02.circ as structural Verilog: 1 circuit, main circuit 2
module _2 (
  input  A,
  input  B,
  input  C,
  input  D,
  output F
);

  wire not_1_out, not_2_out, or_1_out, or_2_out, or_3_out;

  not not_1 (not_1_out, C);
  not not_2 (not_2_out, A);
  or or_1 (or_1_out, not_2_out, D);
  or or_2 (or_2_out, not_1_out, D);
  or or_3 (or_3_out, not_2_out, B, C);
  and and_1 (F, or_3_out, or_1_out, or_2_out);

  // Notes on the sheet:
  //   2. Simplified version of F
endmodule
