// Logisim project Problem-03.circ as structural Verilog: 1 circuit, main circuit 3
module _3 (
  input  in_1,
  output MSB_C,
  output B,
  output LSB_A
);

  wire A_qn, and_1_out, and_2_out, and_3_out, and_4_out, B_qn, CLK_out, or_1_out, or_2_out, or_3_out;

  or or_1 (or_1_out, and_1_out, and_2_out);
  Clock CLK (.out(CLK_out));
  and and_1 (and_1_out, LSB_A, B);
  and and_2 (and_2_out, A_qn, B_qn);
  T_Flip_Flop A (.clk(CLK_out), .T(or_1_out), .Q(LSB_A), .Qn(A_qn), .en(in_1));  // open: preset, reset
  and and_3 (and_3_out, MSB_C, LSB_A);
  and and_4 (and_4_out, A_qn, B);
  T_Flip_Flop u_B (.clk(CLK_out), .T(or_2_out), .Q(B), .Qn(B_qn), .en(in_1));  // open: preset, reset
  or or_2 (or_2_out, and_3_out, and_4_out);
  or or_3 (or_3_out, B_qn, A_qn);
  T_Flip_Flop C (.clk(CLK_out), .T(or_3_out), .Q(MSB_C), .en(in_1));  // open: Qn, preset, reset

  // Notes on the sheet:
  //   3.Design a counter that counts 1,5,3,2,4,1 by using T flip-flops
endmodule
