// Logisim project 1803163.circ as structural Verilog: 4 circuits, main circuit Lab task(NAND Gate)
module Lab_task_NAND_Gate (
  input  a,
  input  b,
  input  c,
  input  d
);

  wire and_1_out, not_1_out;

  and and_1 (and_1_out, a, b, c, d);
  LED led_1 (.in(and_1_out));
  not not_1 (not_1_out, and_1_out);
  LED led_2 (.in(not_1_out));

  // Notes on the sheet:
  //   NAND Gate
  //   g
  //   f
endmodule

module AND_Gate (
  input  a,
  input  b,
  input  c,
  input  d,
  input  e
);

  wire and_1_out;

  and and_1 (and_1_out, a, b, c, d, e);
  LED led_1 (.in(and_1_out));

  // Notes on the sheet:
  //   AND Gate
  //   g
endmodule

module OR_Gate (
  input  a,
  input  b,
  input  c,
  input  d,
  input  e
);

  wire or_1_out;

  LED led_1 (.in(or_1_out));
  or or_1 (or_1_out, e, d, c, b, a);

  // Notes on the sheet:
  //   OR Gate
  //   g
endmodule

module NOT_Gate (
  input  a
);

  wire not_1_out;

  not not_1 (not_1_out, a);
  LED led_1 (.in(not_1_out));

  // Notes on the sheet:
  //   NOT Gate
  //   g
endmodule
