// Logisim project 1803163.circ as structural Verilog: 3 circuits, main circuit 4.1.1(drag & drop)
module _4_1_1_drag___drop (
  input  a,
  input  b,
  input  c,
  input  d
);

  wire m0_out, m1_out, m2_out, m3_out, m4_out, m5_out, m6_out, m7_out, not_1_out, not_2_out, not_3_out,
       not_4_out, or_1_out;

  not not_1 (not_1_out, a);
  not not_2 (not_2_out, b);
  not not_3 (not_3_out, c);
  not not_4 (not_4_out, d);
  and m0 (m0_out, not_1_out, not_2_out, not_3_out, not_4_out);
  and m1 (m1_out, not_1_out, not_2_out, c, not_4_out);
  and m2 (m2_out, not_1_out, not_2_out, c, d);
  and m3 (m3_out, not_1_out, b, not_3_out, not_4_out);
  or or_1 (or_1_out, m0_out, m1_out, m2_out, m3_out, m4_out, m5_out, m6_out, m7_out);
  and m4 (m4_out, not_1_out, b, c, not_4_out);
  and m5 (m5_out, a, not_2_out, c, not_4_out);
  LED led_1 (.in(or_1_out));
  and m6 (m6_out, a, b, c, not_4_out);
  and m7 (m7_out, a, b, c, d);

  // Notes on the sheet:
  //   4.1.1-(Drag & drop) Implement Various Logic functions (For example F(a,b,c,d) = SOP(0,2,3,4,6,10,14,15)
  //   F
endmodule

module _4_1_2_analyse_circuit (
  input  a,
  input  b,
  input  c,
  input  d,
  output F
);

  wire and_1_out, and_2_out, and_3_out, and_4_out, not_1_out, not_2_out, not_3_out, not_4_out, not_5_out;

  not not_1 (not_1_out, a);
  and and_1 (and_1_out, not_1_out, not_2_out);
  not not_2 (not_2_out, d);
  not not_3 (not_3_out, a);
  not not_4 (not_4_out, b);
  and and_2 (and_2_out, not_3_out, not_4_out, c);
  and and_3 (and_3_out, c, not_5_out);
  not not_5 (not_5_out, d);
  and and_4 (and_4_out, a, b, c);
  or or_1 (F, and_1_out, and_2_out, and_3_out, and_4_out);

  // Notes on the sheet:
  //   4.1.2-(Analyse) Implement Various Logic functions (For example F(a,b,c,d) = SOP(0,2,3,4,6,10,14,15)
  //   )
endmodule

module _4_2 (
  input  a,
  input  b,
  input  c,
  input  d
);

  wire and_1_out, and_2_out, and_3_out, and_4_out, not_1_out, not_2_out, not_3_out, not_4_out, not_5_out,
       or_1_out;

  not not_1 (not_1_out, a);
  and and_1 (and_1_out, not_1_out, not_2_out);
  not not_2 (not_2_out, d);
  not not_3 (not_3_out, a);
  not not_4 (not_4_out, b);
  and and_2 (and_2_out, not_3_out, not_4_out, c);
  buf and_3 (and_3_out, not_5_out);  // AND_Gate
  not not_5 (not_5_out, d);
  and and_4 (and_4_out, a, b, c);
  or or_1 (or_1_out, and_1_out, and_2_out, and_3_out, and_4_out);
  LED led_1 (.in(or_1_out));

  // Notes on the sheet:
  //   4.2-Verify the result of simplifiied version of F in 1.
  //   F
endmodule
