// Logisim project 1803163.circ as structural Verilog: 5 circuits, main circuit 5.1.1
module _5_1_1 (
  input  X,
  input  Y
);

  wire and_1_out, and_2_out, and_3_out, not_1_out, not_2_out, or_1_out;

  not not_1 (not_1_out, X);
  not not_2 (not_2_out, Y);
  and and_1 (and_1_out, X, not_2_out);
  and and_2 (and_2_out, not_1_out, Y);
  or or_1 (or_1_out, and_2_out, and_1_out);
  and and_3 (and_3_out, X, Y);
  LED led_1 (.in(and_3_out));
  LED led_2 (.in(or_1_out));

  // Notes on the sheet:
  //   5.1.1 The Half Adder Circuit(using the basic gates)
  //   S
  //   C
endmodule

module _5_1_2 (
  input  X,
  input  Y
);

  wire and_1_out, xor_1_out;

  and and_1 (and_1_out, X, Y);
  xor xor_1 (xor_1_out, X, Y);
  LED led_1 (.in(and_1_out));
  LED led_2 (.in(xor_1_out));

  // Notes on the sheet:
  //   5.1.2 The Half Adder Circuit(using the universal gates)
  //   C
  //   S
endmodule

module _5_2_1 (
  input  X,
  input  Y,
  input  Z
);

  wire and_1_out, and_2_out, and_3_out, and_4_out, and_5_out, and_6_out, and_7_out, not_1_out, not_2_out,
       not_3_out, not_4_out, not_5_out, not_6_out, or_1_out, or_2_out;

  not not_1 (not_1_out, X);
  not not_2 (not_2_out, Y);
  not not_3 (not_3_out, X);
  not not_4 (not_4_out, Z);
  not not_5 (not_5_out, Y);
  not not_6 (not_6_out, Z);
  and and_1 (and_1_out, not_1_out, not_2_out, Z);
  and and_2 (and_2_out, not_3_out, Y, not_4_out);
  and and_3 (and_3_out, X, not_5_out, not_6_out);
  and and_4 (and_4_out, Z, Y, X);
  and and_5 (and_5_out, X, Y);
  and and_6 (and_6_out, X, Z);
  and and_7 (and_7_out, Y, Z);
  or or_1 (or_1_out, and_1_out, and_2_out, and_3_out, and_4_out);
  or or_2 (or_2_out, and_5_out, and_6_out, and_7_out);
  LED led_1 (.in(or_1_out));
  LED led_2 (.in(or_2_out));

  // Notes on the sheet:
  //   5.2.1 The Full Adder Circuit(using the basic gates)
  //   S
  //   C
endmodule

module _5_2_2 (
  input  X,
  input  y,
  input  Z
);

  wire and_1_out, and_2_out, and_3_out, or_1_out, xor_1_out;

  and and_1 (and_1_out, X, y);
  and and_2 (and_2_out, X, Z);
  and and_3 (and_3_out, y, Z);
  ExactlyOne xor_1 (.out(xor_1_out), .in0(X), .in1(y), .in2(Z));
  LED led_1 (.in(xor_1_out));
  or or_1 (or_1_out, and_1_out, and_2_out, and_3_out);
  LED led_2 (.in(or_1_out));

  // Notes on the sheet:
  //   5.2.2 The Full Adder Circuit(using the universal gates)
  //   S
  //   C
endmodule

module _5_3 (
  input  x,
  input  y,
  input  z
);

  wire and_1_out, and_2_out, or_1_out, xor_1_out, xor_2_out;

  and and_1 (and_1_out, x, y);
  xor xor_1 (xor_1_out, x, y);
  and and_2 (and_2_out, xor_1_out, z);
  xor xor_2 (xor_2_out, xor_1_out, z);
  or or_1 (or_1_out, and_1_out, and_2_out);
  LED led_1 (.in(or_1_out));
  LED led_2 (.in(xor_2_out));

  // Notes on the sheet:
  //   5.3 The Full Adder Circuit by Using Half Adder 
  //   S 
  //   C
endmodule
