// Logisim project 1803163.circ as structural Verilog: 2 circuits, main circuit 6.1
module _6_1 (
  input  X,
  input  y,
  input  z
);

  wire and_1_out, and_2_out, and_3_out, and_4_out, and_5_out, not_1_out, not_2_out, not_3_out, or_1_out,
       or_2_out;

  not not_1 (not_1_out, z);
  and and_1 (and_1_out, not_1_out, z);
  not not_2 (not_2_out, X);
  not not_3 (not_3_out, y);
  or or_1 (or_1_out, not_1_out, z);
  and and_2 (and_2_out, not_2_out, not_3_out, z);
  and and_3 (and_3_out, not_2_out, y, not_1_out);
  and and_4 (and_4_out, X, not_3_out, and_1_out);
  and and_5 (and_5_out, X, y, or_1_out);
  or or_2 (or_2_out, and_2_out, and_3_out, and_4_out, and_5_out);
  LED led_1 (.in(or_2_out));

  // Notes on the sheet:
  //   6.1: Verifying various multiplexers input and output
  //   f(x,y,z)=SOP(1,2,6,7)
endmodule

module _6_2 (
  input  D3,
  input  D2,
  input  D1,
  input  D0
);

  wire and_1_out, not_1_out, or_1_out, or_2_out, or_3_out;

  not not_1 (not_1_out, D2);
  or or_1 (or_1_out, D3, D2);
  and and_1 (and_1_out, not_1_out, D1);
  or or_2 (or_2_out, or_1_out, D1, D0);
  or or_3 (or_3_out, D3, and_1_out);
  LED led_1 (.in(or_3_out));
  LED led_2 (.in(or_1_out));
  LED led_3 (.in(or_2_out));

  // Notes on the sheet:
  //   6.2: Verifying various encoders input and output
  //   y
  //   x
  //   V
endmodule
