// Logisim project 1803163.circ as structural Verilog: 8 circuits, main circuit 7.1.1
module _7_1_1 (
  input  S,
  input  R,
  output Q_prime,
  output Q
);

  wire and_1_out, and_2_out, clock_1_out;

  Clock clock_1 (.out(clock_1_out));
  and and_1 (and_1_out, S, clock_1_out);
  and and_2 (and_2_out, clock_1_out, R);
  nor nor_1 (Q_prime, and_1_out, Q);
  nor nor_2 (Q, Q_prime, and_2_out);

  // Notes on the sheet:
  //   CLK
  //   7.1.1: SR FF using NOR Latch
endmodule

module _7_1_2 (
  input  S,
  input  R,
  output Q_prime,
  output Q
);

  wire clock_1_out, nand_1_out, nand_2_out;

  Clock clock_1 (.out(clock_1_out));
  nand nand_1 (nand_1_out, S, clock_1_out);
  nand nand_2 (nand_2_out, clock_1_out, R);
  nand nand_3 (Q_prime, nand_1_out, Q);
  nand nand_4 (Q, Q_prime, nand_2_out);

  // Notes on the sheet:
  //   CLK
  //   7.1.2: SR FF using NAND Latch
endmodule

module _7_2_1 (
  input  J,
  input  K,
  output Q_prime,
  output Q
);

  wire and_1_out, and_2_out, clock_1_out;

  Clock clock_1 (.out(clock_1_out));
  and and_1 (and_1_out, Q_prime, J, clock_1_out);
  and and_2 (and_2_out, clock_1_out, K, Q);
  nor nor_1 (Q_prime, and_1_out, Q);
  nor nor_2 (Q, Q_prime, and_2_out);

  // Notes on the sheet:
  //   CLK
  //   7.2.1: JK FF using NOR Latch
endmodule

module _7_2_2 (
  input  J,
  input  K,
  output Q_prime,
  output Q
);

  wire clock_1_out, nand_1_out, nand_2_out;

  Clock clock_1 (.out(clock_1_out));
  nand nand_1 (nand_1_out, Q_prime, J, clock_1_out);
  nand nand_2 (nand_2_out, clock_1_out, K, Q);
  nand nand_3 (Q_prime, nand_1_out, Q);
  nand nand_4 (Q, Q_prime, nand_2_out);

  // Notes on the sheet:
  //   CLK
  //   7.2.2: JK FF using NAND Latch
endmodule

module _7_3_1 (
  input  D,
  output Q,
  output Q_prime
);

  wire and_1_out, and_2_out, clock_1_out, not_1_out;

  Clock clock_1 (.out(clock_1_out));
  not not_1 (not_1_out, D);
  and and_1 (and_1_out, D, clock_1_out);
  and and_2 (and_2_out, clock_1_out, not_1_out);
  nor nor_1 (Q, and_1_out, Q_prime);
  nor nor_2 (Q_prime, Q, and_2_out);

  // Notes on the sheet:
  //   CLK
  //   7.3.1: D FF using NOR Latch
endmodule

module _7_3_2 (
  input  D,
  output Q,
  output Q_prime
);

  wire clock_1_out, nand_1_out, nand_2_out, not_1_out;

  Clock clock_1 (.out(clock_1_out));
  not not_1 (not_1_out, D);
  nand nand_1 (nand_1_out, D, clock_1_out);
  nand nand_2 (nand_2_out, clock_1_out, not_1_out);
  nand nand_3 (Q, nand_1_out, Q_prime);
  nand nand_4 (Q_prime, Q, nand_2_out);

  // Notes on the sheet:
  //   CLK
  //   7.3.2: D FF using NAND Latch
endmodule

module _7_4_1 (
  input  T,
  output Q,
  output Q_prime
);

  wire and_1_out, and_2_out, clock_1_out;

  Clock clock_1 (.out(clock_1_out));
  and and_1 (and_1_out, Q, T, clock_1_out);
  and and_2 (and_2_out, clock_1_out, T, Q_prime);
  nor nor_1 (Q, and_1_out, Q_prime);
  nor nor_2 (Q_prime, Q, and_2_out);

  // Notes on the sheet:
  //   CLK
  //   7.4.1: T FF using NOR Latch
endmodule

module _7_4_2 (
  input  T,
  output Q,
  output Q_prime
);

  wire clock_1_out, nand_1_out, nand_2_out;

  Clock clock_1 (.out(clock_1_out));
  nand nand_1 (nand_1_out, Q, T, clock_1_out);
  nand nand_2 (nand_2_out, clock_1_out, T, Q_prime);
  nand nand_3 (Q, nand_1_out, Q_prime);
  nand nand_4 (Q_prime, Q, nand_2_out);

  // Notes on the sheet:
  //   CLK
  //   7.4.2: T FF using NAND Latch
endmodule
