// Logisim project 1803163.circ as structural Verilog: 4 circuits, main circuit 8.1
module _8_1 (
  input  S,
  input  R,
  input  SET,
  input  in_4,
  input  in_5,
  output Q,
  output Q_prime
);

  wire clock_1_out;

  Clock clock_1 (.out(clock_1_out));
  S_R_Flip_Flop s_r_ff_1 (.S(S), .clk(clock_1_out), .R(R), .Q(Q), .Qn(Q_prime), .preset(SET), .reset(in_4), .en(in_5));

  // Notes on the sheet:
  //   CLK
  //   ENABLE
  //   8.1: SR FF using module
  //   RESET
endmodule

module _8_2 (
  input  J,
  input  K,
  input  SET,
  input  RESET,
  input  in_5,
  output Q,
  output Q_prime
);

  wire clock_1_out;

  Clock clock_1 (.out(clock_1_out));
  J_K_Flip_Flop j_k_ff_1 (.J(J), .clk(clock_1_out), .K(K), .Q(Q), .Qn(Q_prime), .preset(SET), .en(in_5), .reset(RESET));

  // Notes on the sheet:
  //   CLK
  //   ENABLE
  //   8.2: JK FF using module
endmodule

module _8_3 (
  input  D,
  input  SET,
  input  RESET,
  input  in_4,
  output Q,
  output Q_prime
);

  wire clock_1_out;

  Clock clock_1 (.out(clock_1_out));
  D_Flip_Flop d_ff_1 (.clk(clock_1_out), .D(D), .Q(Q), .Qn(Q_prime), .preset(SET), .en(in_4), .reset(RESET));

  // Notes on the sheet:
  //   CLK
  //   ENABLE
  //   8.3: D FF using module
endmodule

module _8_4 (
  input  T,
  input  SET,
  input  RESET,
  input  ENABLE,
  output Q,
  output Q_prime
);

  wire clock_1_out;

  Clock clock_1 (.out(clock_1_out));
  T_Flip_Flop t_ff_1 (.clk(clock_1_out), .T(T), .Q(Q), .Qn(Q_prime), .preset(SET), .reset(RESET), .en(ENABLE));

  // Notes on the sheet:
  //   CLK
  //   8.4: T FF using module
endmodule
