// Logisim project 1803163.circ as structural Verilog: 2 circuits, main circuit 9.1
module _9_1 (
  input  JK,
  input  En,
  output MSB_C,
  output B,
  output LSB_A
);

  wire CLK_out;

  Clock CLK (.out(CLK_out));
  J_K_Flip_Flop #(.trigger("falling")) A (
    .J(JK), .clk(CLK_out), .K(JK), .Q(LSB_A), .en(En));  // open: Qn, preset, reset
  J_K_Flip_Flop #(.trigger("falling")) u_B (.J(JK), .clk(LSB_A), .K(JK), .Q(B), .en(En));  // open: Qn, preset, reset
  J_K_Flip_Flop #(.trigger("falling")) C (.J(JK), .clk(B), .K(JK), .Q(MSB_C), .en(En));  // open: Qn, preset, reset

  // Notes on the sheet:
  //   9.1: 3-bit Asynchronous Counter using JK FF
endmodule

module _9_2 (
  input  INPUT,
  input  En,
  output MSB_C,
  output B,
  output LSB_A
);

  wire and_1_out, and_2_out, and_3_out, CLK_out, d_ff_1_qn, j_k_ff_1_qn, or_1_out, t_ff_1_qn;

  Clock CLK (.out(CLK_out));
  J_K_Flip_Flop j_k_ff_1 (
    .J(INPUT), .clk(CLK_out), .K(INPUT), .Q(LSB_A), .Qn(j_k_ff_1_qn), .en(En));  // open: preset, reset
  T_Flip_Flop t_ff_1 (.clk(CLK_out), .T(LSB_A), .Q(B), .Qn(t_ff_1_qn), .en(En));  // open: preset, reset
  and and_1 (and_1_out, MSB_C, t_ff_1_qn);
  and and_2 (and_2_out, B, LSB_A, d_ff_1_qn);
  and and_3 (and_3_out, MSB_C, B, j_k_ff_1_qn);
  or or_1 (or_1_out, and_1_out, and_3_out, and_2_out);
  D_Flip_Flop d_ff_1 (.clk(CLK_out), .D(or_1_out), .Q(MSB_C), .Qn(d_ff_1_qn), .en(En));  // open: preset, reset

  // Notes on the sheet:
  //   9.2: 3-bit Synchronous Counter using various(JK,T,D) FF
endmodule
